// Logisim project capstone-circuit.circ as structural Verilog: 5 circuits, main circuit main
module main (
);

  _1bit_ALU u_1bit_alu_1 ();  // open: INVA, A, ENA, B, ENB, F0, F1, Output, Carry_Out, Carry_In
endmodule

module Logical_Unit (
  input  in_1,
  input  in_2,
  input  in_3,
  input  in_4,
  input  in_5,
  output out_6,
  output out_7,
  output out_8,
  output out_9,
  output out_10
);

  wire A___B_out, AB_out, Not_B_out;

  and AB (AB_out, in_1, in_2);
  or A___B (A___B_out, in_1, in_2);
  not Not_B (Not_B_out, in_2);
  and and_1 (out_6, AB_out, in_3);
  and and_2 (out_7, A___B_out, in_4);
  and and_3 (out_8, Not_B_out, in_5);

  assign out_9 = in_1;
  assign out_10 = in_2;
endmodule

module Full_Adder (
  input  in_1,
  input  in_2,
  input  in_3,
  input  in_4,
  output out_5,
  output out_6
);

  wire and_1_out, and_2_out, xor_1_out, xor_2_out;

  and and_1 (and_1_out, in_4, in_3, in_2);
  or or_1 (out_6, and_1_out, and_2_out);
  xor xor_1 (xor_1_out, in_2, in_3);
  and and_2 (and_2_out, in_4, xor_1_out, in_1);
  xor xor_2 (xor_2_out, in_1, xor_1_out);
  and and_3 (out_5, xor_2_out, in_4);
endmodule

module Decoder (
  input  in_1,
  input  in_2,
  output out_3,
  output out_4,
  output out_5,
  output out_6
);

  wire not_1_out, not_2_out;

  not not_1 (not_1_out, in_1);
  not not_2 (not_2_out, in_2);
  and and_1 (out_3, not_1_out, not_2_out);
  and and_2 (out_4, not_1_out, in_2);
  and and_3 (out_5, in_1, not_2_out);
  and and_4 (out_6, in_1, in_2);
endmodule

module _1bit_ALU (
  input  INVA,
  input  A,
  input  Carry_In,
  input  ENA,
  input  B,
  input  ENB,
  input  F0,
  input  F1,
  output Output,
  output Carry_Out
);

  wire and_1_out, and_2_out, DC_out_3, DC_out_4, DC_out_5, DC_out_6, FA_out_5, FA_out_6, LU_out_6, LU_out_7,
       LU_out_8, LU_out_9, LU_out_10, xor_1_out;

  and and_1 (and_1_out, A, ENA);
  xor xor_1 (xor_1_out, INVA, and_1_out);
  and and_2 (and_2_out, B, ENB);
  Logical_Unit LU (
    .in_1(xor_1_out), .in_2(and_2_out), .out_6(LU_out_6), .out_7(LU_out_7), .out_8(LU_out_8),
    .out_9(LU_out_9), .out_10(LU_out_10), .in_3(DC_out_3), .in_4(DC_out_4), .in_5(DC_out_5));
  Decoder DC (.out_3(DC_out_3), .out_4(DC_out_4), .out_5(DC_out_5), .out_6(DC_out_6), .in_1(F0), .in_2(F1));
  Full_Adder FA (
    .in_2(LU_out_10), .in_3(LU_out_9), .in_4(DC_out_6), .in_1(Carry_In), .out_5(FA_out_5), .out_6(FA_out_6));
  or or_1 (Output, LU_out_6, LU_out_7, LU_out_8, FA_out_5);
endmodule
